// Logisim project CPU1-RCAGAMEZ.circ as structural Verilog: 7 circuits, main circuit main
module main (
);

  wire CLK, debugcomponent_1_aand, debugcomponent_1_add, debugcomponent_1_addi, debugcomponent_1_beq,
       debugcomponent_1_bnq, debugcomponent_1_jump, debugcomponent_1_load, debugcomponent_1_none,
       debugcomponent_1_oor, debugcomponent_1_store, debugcomponent_1_sub, Rst, uc_1_alusrc, uc_1_beq,
       uc_1_bne, uc_1_jump, uc_1_memread, uc_1_memtoreg, uc_1_memwrite, uc_1_regdst, uc_1_regwrite;
  wire [1:0] uc_1_alu, ucalu_1_output;
  wire [4:0] id_1_rd, id_1_rs, id_1_rt, id_1_shamt;
  wire [5:0] FUNC, OPCODE;
  wire [15:0] id_1_inmediate;
  wire [23:0] adder_1_out, Iter;
  wire [25:0] id_1_jumadd;
  wire [31:0] ram_1_dout;

  RAM #(.addrWidth(24), .dataWidth(32), .enables("line")) ram_1 (.addr(Iter), .dout(ram_1_dout));  // open: we, clk, din
  Button button_1 (.out(Rst));
  Clock clock_1 (.out(CLK));
  Register #(.width(24)) register_1 (.D(adder_1_out), .Q(Iter), .clk(CLK), .clr(Rst));  // open: en
  Adder #(.width(24)) adder_1 (.a(Iter), .b(24'h1), .out(adder_1_out));  // open: cin, cout
  ID id_1 (
    .INPUTID(ram_1_dout), .Funct(FUNC), .Shamt(id_1_shamt), .Inmediate(id_1_inmediate), .RD(id_1_rd),
    .RT(id_1_rt), .RS(id_1_rs), .OPCODE(OPCODE), .JumAdd(id_1_jumadd));
  // Probe on FUNC
  // Probe on id_1_shamt
  // Probe on id_1_inmediate
  // Probe on id_1_rd
  // Probe on id_1_rt
  // Probe on id_1_rs
  // Probe on id_1_jumadd
  // Probe on OPCODE
  // Probe on debugcomponent_1_addi
  DebugComponent debugcomponent_1 (
    .opCode(OPCODE), .funct(FUNC), .Addi(debugcomponent_1_addi), .Load(debugcomponent_1_load),
    .Store(debugcomponent_1_store), .BEQ(debugcomponent_1_beq), .BNQ(debugcomponent_1_bnq),
    .Jump(debugcomponent_1_jump), .None(debugcomponent_1_none), .Add(debugcomponent_1_add),
    .Sub(debugcomponent_1_sub), .AAnd(debugcomponent_1_aand), .OOr(debugcomponent_1_oor));
  // Probe on debugcomponent_1_load
  // Probe on debugcomponent_1_store
  // Probe on debugcomponent_1_beq
  // Probe on debugcomponent_1_bnq
  // Probe on debugcomponent_1_jump
  // Probe on debugcomponent_1_none
  // Probe on debugcomponent_1_add
  // Probe on debugcomponent_1_sub
  // Probe on debugcomponent_1_aand
  // Probe on debugcomponent_1_oor
  // Probe on uc_1_regdst
  UC uc_1 (
    .opcode(OPCODE), .regdst(uc_1_regdst), .regwrite(uc_1_regwrite), .jump(uc_1_jump), .beq(uc_1_beq),
    .bne(uc_1_bne), .alusrc(uc_1_alusrc), .memToReg(uc_1_memtoreg), .memRead(uc_1_memread),
    .memWrite(uc_1_memwrite), .ALU(uc_1_alu));
  // Probe on uc_1_regwrite
  // Probe on uc_1_jump
  // Probe on uc_1_beq
  // Probe on uc_1_bne
  // Probe on uc_1_alusrc
  // Probe on uc_1_memtoreg
  // Probe on uc_1_memread
  // Probe on uc_1_memwrite
  // Probe on uc_1_alu
  // Probe on ucalu_1_output
  UCALU ucalu_1 (.ALUOP(uc_1_alu), .FUNC(FUNC), .OUTPUT(ucalu_1_output));
endmodule

module ID (
  input  [31:0] INPUTID,
  output [5:0] Funct,
  output [4:0] Shamt,
  output [15:0] Inmediate,
  output [4:0] RD,
  output [4:0] RT,
  output [4:0] RS,
  output [5:0] OPCODE,
  output [25:0] JumAdd
);

  wire J, not_1_out, or_1_out, R;

  Comparator #(.width(6)) comparator_1 (.a(INPUTID[31:26]), .b(6'b000010), .eq(J));  // open: gt, lt
  Multiplexer #(.width(26)) multiplexer_1 (.in1(INPUTID[25:0]), .out(JumAdd), .sel(J));  // open: in0
  or or_1 (or_1_out, R, J);
  Multiplexer #(.width(16)) multiplexer_2 (.in1(INPUTID[15:0]), .out(Inmediate), .sel(not_1_out));  // open: in0
  not not_1 (not_1_out, or_1_out);
  Comparator #(.width(6)) comparator_2 (.a(INPUTID[31:26]), .b({6{1'b0}}), .eq(R));  // open: gt, lt
  Multiplexer #(.width(16)) multiplexer_3 (.in1(INPUTID[15:0]), .out({RD, Shamt, Funct}), .sel(R));  // open: in0

  assign OPCODE = INPUTID[31:26];
  assign RS = INPUTID[25:21];
  assign RT = INPUTID[20:16];

  // Other names for the same wires on the sheet: OP[5:0] = INPUTID[31:26]; JUMP[25:0] = JumAdd

  // Notes on the sheet:
  //   Cuando es J
  //   Cuando es R
endmodule

module UC (
  input  [5:0] opcode,
  output regdst,
  output regwrite,
  output jump,
  output beq,
  output bne,
  output alusrc,
  output memToReg,
  output memRead,
  output memWrite,
  output [1:0] ALU
);

  wire and_2_out, and_3_out, not_1_out, not_2_out, not_3_out, not_4_out;

  not not_1 (not_1_out, opcode[3]);
  not not_2 (not_2_out, opcode[2]);
  not not_3 (not_3_out, opcode[1]);
  not not_4 (not_4_out, opcode[0]);
  and and_1 (regdst, not_1_out, not_2_out, not_3_out);
  and and_2 (and_2_out, not_2_out, not_3_out);
  and and_3 (and_3_out, opcode[5], not_1_out);
  and and_4 (jump, opcode[1], not_4_out);
  and and_5 (beq, not_3_out, opcode[0]);
  and and_6 (bne, opcode[2], not_4_out);
  or or_1 (alusrc, opcode[3], opcode[5]);
  and and_7 (memToReg, opcode[5], not_1_out);
  and and_8 (memRead, opcode[5], not_1_out);
  and and_9 (memWrite, opcode[3], opcode[1]);
  and and_10 (ALU[1], not_1_out, not_2_out, not_3_out);
  or or_2 (regwrite, and_2_out, and_3_out);

  assign ALU[0] = opcode[2];
endmodule

module DebugComponent (
  input  [5:0] opCode,
  input  [5:0] funct,
  output Addi,
  output Load,
  output Store,
  output BEQ,
  output BNQ,
  output Jump,
  output None,
  output Add,
  output Sub,
  output AAnd,
  output OOr
);

  wire nonoOrR;

  debugStep1 debugstep1_1 (
    .opcode(opCode), .noneOrR(nonoOrR), .addi(Addi), .load(Load), .store(Store), .beq(BEQ), .bnq(BNQ),
    .jump(Jump));
  debugStep2 debugstep2_1 (.noneOrR(nonoOrR), .funct(funct), .none(None), .add(Add), .sub(Sub), .aand(AAnd), .oor(OOr));
endmodule

module debugStep1 (
  input  [5:0] opcode,
  output noneOrR,
  output addi,
  output load,
  output store,
  output beq,
  output bnq,
  output jump
);

  wire not_1_out, not_2_out, not_3_out, not_4_out, not_5_out, not_6_out;

  not not_1 (not_1_out, opcode[5]);
  not not_2 (not_2_out, opcode[4]);
  not not_3 (not_3_out, opcode[3]);
  not not_4 (not_4_out, opcode[2]);
  not not_5 (not_5_out, opcode[1]);
  not not_6 (not_6_out, opcode[0]);
  and and_1 (noneOrR, not_1_out, not_2_out, not_3_out, not_4_out, not_5_out, not_6_out);
  and and_2 (addi, not_1_out, not_2_out, opcode[3], not_4_out, not_5_out, not_6_out);
  and and_3 (load, opcode[5], not_2_out, not_3_out, not_4_out, opcode[1], opcode[0]);
  and and_4 (store, opcode[5], not_2_out, opcode[3], not_4_out, opcode[1], opcode[0]);
  and and_5 (beq, not_1_out, not_2_out, not_3_out, opcode[2], not_5_out, not_6_out);
  and and_6 (bnq, not_1_out, not_2_out, not_3_out, opcode[2], not_5_out, opcode[0]);
  and and_7 (jump, not_1_out, not_2_out, not_3_out, not_4_out, opcode[1], not_6_out);
endmodule

module debugStep2 (
  input  noneOrR,
  input  [5:0] funct,
  output none,
  output add,
  output sub,
  output aand,
  output oor
);

  wire not_1_out, not_2_out, not_3_out, not_4_out, not_5_out, not_6_out;

  not not_1 (not_1_out, funct[5]);
  not not_2 (not_2_out, funct[4]);
  not not_3 (not_3_out, funct[3]);
  not not_4 (not_4_out, funct[2]);
  not not_5 (not_5_out, funct[1]);
  not not_6 (not_6_out, funct[0]);
  and and_1 (none, noneOrR, not_1_out, not_2_out, not_3_out, not_4_out, not_5_out, not_6_out);
  and and_2 (add, noneOrR, funct[5], not_2_out, not_3_out, not_4_out, not_5_out, not_6_out);
  and and_3 (sub, noneOrR, funct[5], not_2_out, not_3_out, not_4_out, funct[1], not_6_out);
  and and_4 (aand, noneOrR, funct[5], not_2_out, not_3_out, funct[2], not_5_out, not_6_out);
  and and_5 (oor, noneOrR, funct[5], not_2_out, not_3_out, funct[2], not_5_out, funct[0]);
endmodule

module UCALU (
  input  [1:0] ALUOP,
  input  [5:0] FUNC,
  output [1:0] OUTPUT
);

  wire and_1_out, and_2_out, and_3_out, and_4_out, not_1_out, not_2_out, not_3_out, not_4_out, not_5_out,
       not_6_out, not_7_out;

  not not_1 (not_1_out, ALUOP[1]);
  not not_2 (not_2_out, ALUOP[0]);
  not not_3 (not_3_out, FUNC[4]);
  not not_4 (not_4_out, FUNC[3]);
  not not_5 (not_5_out, FUNC[2]);
  not not_6 (not_6_out, FUNC[1]);
  not not_7 (not_7_out, FUNC[0]);
  or or_1 (OUTPUT[1], not_1_out, and_1_out);
  and and_1 (and_1_out, not_2_out, FUNC[5], not_3_out, not_4_out, not_5_out, not_7_out);
  and and_2 (and_2_out, ALUOP[1], not_2_out, FUNC[5], not_3_out, not_4_out, not_5_out, FUNC[1], not_7_out);
  and and_3 (and_3_out, ALUOP[1], not_2_out, FUNC[5], not_3_out, not_4_out, FUNC[2], not_6_out, FUNC[0]);
  or or_2 (OUTPUT[0], and_2_out, and_3_out, and_4_out);
  and and_4 (and_4_out, not_1_out, ALUOP[0]);
endmodule
